# Fritzing sketch Schematic (saved by Fritzing 0.8.7b)
breadboards: 1

parts:
  Part1 = Arduino Uno (Rev3)
  D1 = Rectifier Diode [part_number=1N4001 package="300 mil [THT]"]
  S1 = Pushbutton [package="[THT]"]
  R1 = Resistor [tolerance=±5% resistance=10k package="1206 [SMD]"]
  U2 = Voltage Regulator - 5V [package="DPak [SMD]"]
  J1 = Basic Servo
  J2 = Basic Servo
  Power_plug1 = Power plug

nets:
  N1: Part1.D13/SCK, S1.Pin_1, S1.Pin_2, R1.Pin_0
  N2: Part1.D2, J2.pulse
  N3: Part1.D3_PWM, J1.pulse
  GND: Part1.GND, R1.Pin_1, U2.GND, J1.gnd, J2.gnd, Power_plug1.GND
  N4: Part1.VIN, D1.cathode
  N5: D1.anode, U2.input_voltage, Power_plug1.VCC
  VCC: S1.Pin_3, S1.Pin_4, U2.output_voltage, J1.vcc, J2.vcc

notes:
  bus
  goes to QTR
  sensor
  Power to QTR
  to QTR LED pin
  Power supply
  (Mines 10.8V)
